// Logisim project Homework2_Exercise_5.12.circ as structural Verilog: 3 circuits, main circuit main
module main (
  input  [1:0] ALU_CON,
  input  [31:0] A,
  input  [31:0] B,
  output [31:0] D_out,
  output Z,
  output N,
  output C,
  output V
);

  // Probe on A
  // Probe on A
  // Probe on A
  _32_bit_ALU_outputflags u_32_bit_alu_outputflags_1 (
    .in_1(ALU_CON), .B(B), .A(A), .out_5(D_out), .Zero(Z), .Negative(N), .Carry(C), .Overflow(V));  // open: Do_Mov
  // Probe on B
  // Probe on B
  // Probe on B
  // Probe on D_out
  // Probe on D_out
  // Probe on D_out
endmodule

module _32_bit_ALU_outputflags (
  input  [1:0] in_1,
  input  [31:0] B,
  input  [31:0] A,
  input  Do_Mov,
  output [31:0] out_5,
  output Zero,
  output Negative,
  output Carry,
  output Overflow
);

  wire n32_bit_adder_1_out_5, not_2_out, xnor_1_out, xor_1_out;
  wire [31:0] and_1_out, multiplexer_1_out, multiplexer_2_out, not_1_out, or_1_out, wormhole;

  Multiplexer #(.width(32), .enable("false")) multiplexer_1 (
    .in0(A), .in1({32{1'b0}}), .out(multiplexer_1_out), .sel(Do_Mov));
  Multiplexer #(.width(32), .disabled(0)) multiplexer_2 (
    .in0(B), .in1(not_1_out), .out(multiplexer_2_out), .sel(in_1[0]), .en(1'b1));
  assign not_1_out = ~B;  // NOT_Gate not_1, 32 bits wide
  xor xor_1 (xor_1_out, B[31], multiplexer_1_out[31]);
  _32_bit_adder u_32_bit_adder_1 (
    .in_2(multiplexer_2_out), .in_3(multiplexer_1_out), .in_1(in_1[0]), .out_5(n32_bit_adder_1_out_5),
    .total(wormhole));
  not not_2 (not_2_out, in_1[1]);
  NotExactlyOne xnor_1 (.out(xnor_1_out), .in0(multiplexer_1_out[31]), .in1(wormhole[31]), .in2(in_1[0]));
  assign and_1_out = B & multiplexer_1_out;  // AND_Gate and_1, 32 bits wide
  assign or_1_out = B | multiplexer_1_out;  // OR_Gate or_1, 32 bits wide
  and and_2 (Carry, n32_bit_adder_1_out_5, not_2_out);
  and and_3 (Overflow, not_2_out, xor_1_out, xnor_1_out);
  Multiplexer #(.select(2), .width(32), .disabled(0)) multiplexer_3 (
    .in0(wormhole), .in1(wormhole), .in2(and_1_out), .in3(or_1_out), .out({Negative, out_5[30:0]}),
    .sel(in_1), .en(1'b1));
  and32_zero and32_zero_1 (.in_1({Negative, out_5[30:0]}), .out_2(Zero));

  assign out_5[31] = Negative;
endmodule

module and32_zero (
  input  [31:0] in_1,
  output out_2
);

  and and_1 (out_2, ~in_1[0], ~in_1[1], ~in_1[2], ~in_1[3], ~in_1[4], ~in_1[5], ~in_1[6], ~in_1[7], ~in_1[8], ~in_1[9], ~in_1[10], ~in_1[11], ~in_1[12], ~in_1[13], ~in_1[14], ~in_1[15], ~in_1[16], ~in_1[17], ~in_1[18], ~in_1[19], ~in_1[20], ~in_1[21], ~in_1[22], ~in_1[23], ~in_1[24], ~in_1[25], ~in_1[26], ~in_1[27], ~in_1[28], ~in_1[29], ~in_1[30], ~in_1[31]);  // AND_Gate
endmodule
