// Logisim project project_4.circ as structural Verilog: 13 circuits, main circuit main
module main (
  input  CLR,
  input  [1:0] Select_Inst
);

  wire C, CLK_out, control_1_alusrc, control_1_branchlink, control_1_bx_2, control_1_do_mov,
       control_1_memreg, control_1_memw, control_1_pcsrc, control_1_regwrite, N, not_1_out, V, Z;
  wire [1:0] control_1_alucontrol, control_1_immsrc, control_1_regsrc;
  wire [3:0] multiplexer_2_out, multiplexer_3_out;
  wire [31:0] adder_1_out, adder_2_out, data__mem_1_out_6, extend_1_out_3, inst_mem_1_rd, multiplexer_1_out,
       multiplexer_4_out, multiplexer_5_out, n32_bit_alu_outputflags_1_out_5, pc_1_out_6, R0, R1, R2, R3, R4,
       R5, R6, R7, R8, R9, R10, R11, R12, R13, R14, R15, regester_file_1_out_13, regester_file_1_out_16;

  // Probe on R0
  // Probe on R4
  // Probe on R8
  // Probe on R12
  Clock CLK (.out(CLK_out));
  // Probe on Select_Inst
  Multiplexer #(.width(32), .enable("false")) multiplexer_1 (
    .in0(adder_1_out), .in1(multiplexer_5_out), .out(multiplexer_1_out), .sel(control_1_pcsrc));
  PC pc_1 (.D(multiplexer_1_out), .CLR(CLR), .R14(R14), .BX(control_1_bx_2), .CLK(CLK_out), .out_6(pc_1_out_6));
  // Probe on R1
  // Probe on R5
  // Probe on R9
  // Probe on R13
  // Probe on R2
  // Probe on R6
  // Probe on R10
  // Probe on R14
  Inst_mem inst_mem_1 (.A(pc_1_out_6), .RD(inst_mem_1_rd), .Selector(Select_Inst));
  Adder #(.width(32)) adder_1 (.a(pc_1_out_6), .b(32'h4), .out(adder_1_out));  // open: cin, cout
  Control control_1 (
    .RD(inst_mem_1_rd[15:12]), .OP(inst_mem_1_rd[27:26]), .Funct(inst_mem_1_rd[25:20]),
    .MemReg(control_1_memreg), .MemW(control_1_memw), .IMMsrc(control_1_immsrc),
    .RegWrite(control_1_regwrite), .REGSrc(control_1_regsrc), .AlUsrc(control_1_alusrc),
    .AlUControl(control_1_alucontrol), .Z(Z), .N(N), .C(C), .V(V), .COND(inst_mem_1_rd[31:28]),
    .PCSrc(control_1_pcsrc), .CLK(CLK_out), .CLR(CLR), .Do_Mov(control_1_do_mov),
    .BranchLink(control_1_branchlink), .BX(inst_mem_1_rd[27:4]), .BX_2(control_1_bx_2));
  // Probe on R3
  // Probe on R7
  // Probe on R11
  // Probe on R15
  Multiplexer #(.width(4), .enable("false")) multiplexer_2 (
    .in0(inst_mem_1_rd[19:16]), .in1(4'b1111), .out(multiplexer_2_out), .sel(control_1_regsrc[0]));
  Adder #(.width(32)) adder_2 (.a(32'h4), .b(adder_1_out), .out(adder_2_out));  // open: cin, cout
  Multiplexer #(.width(4), .enable("false")) multiplexer_3 (
    .in0(inst_mem_1_rd[3:0]), .in1(inst_mem_1_rd[15:12]), .out(multiplexer_3_out), .sel(control_1_regsrc[1]));
  Regester_File regester_file_1 (
    .WD3(multiplexer_5_out), .CLK(CLK_out), .CLR(CLR), .WE(control_1_regwrite), .R0(R0), .R1(R1),
    .A3(inst_mem_1_rd[15:12]), .R2(R2), .R3(R3), .R4(R4), .R5(R5), .R6(R6), .R7(R7), .R8(R8), .R9(R9),
    .R10(R10), .R11(R11), .R12(R12), .R13(R13), .R14(R14), .R15_2(R15), .out_13(regester_file_1_out_13),
    .out_16(regester_file_1_out_16), .A1(multiplexer_2_out), .A2(multiplexer_3_out), .R15(adder_2_out),
    .BranchLink(control_1_branchlink));
  Extend extend_1 (.in_2(inst_mem_1_rd[23:0]), .out_3(extend_1_out_3), .in_1(control_1_immsrc));
  Multiplexer #(.width(32), .enable("false")) multiplexer_4 (
    .in0(regester_file_1_out_16), .in1(extend_1_out_3), .out(multiplexer_4_out), .sel(control_1_alusrc));
  _32_bit_ALU_outputflags u_32_bit_alu_outputflags_1 (
    .in_1(control_1_alucontrol), .B(multiplexer_4_out), .A(regester_file_1_out_13),
    .out_5(n32_bit_alu_outputflags_1_out_5), .Zero(Z), .Negative(N), .Carry(C), .Overflow(V),
    .Do_Mov(control_1_do_mov));
  not not_1 (not_1_out, CLK_out);
  Data__Mem data__mem_1 (
    .CLK(not_1_out), .in_2(n32_bit_alu_outputflags_1_out_5), .in_3(regester_file_1_out_16), .CLR(CLR),
    .out_6(data__mem_1_out_6), .WE(control_1_memw));
  Multiplexer #(.width(32), .enable("false")) multiplexer_5 (
    .in0(n32_bit_alu_outputflags_1_out_5), .in1(data__mem_1_out_6), .out(multiplexer_5_out),
    .sel(control_1_memreg));

  // Notes on the sheet:
  //   WriteData
endmodule

module Regester_File (
  input  BranchLink,
  input  CLK,
  input  CLR,
  input  [31:0] WD3,
  input  WE,
  input  [3:0] A1,
  input  [3:0] A2,
  input  [3:0] A3,
  input  [31:0] R15,
  output [31:0] R0,
  output [31:0] R1,
  output [31:0] R2,
  output [31:0] out_13,
  output [31:0] R3,
  output [31:0] R4,
  output [31:0] out_16,
  output [31:0] R5,
  output [31:0] R6,
  output [31:0] R7,
  output [31:0] R8,
  output [31:0] R9,
  output [31:0] R10,
  output [31:0] R11,
  output [31:0] R12,
  output [31:0] R13,
  output [31:0] R14,
  output [31:0] R15_2
);

  wire _4bit_Decoder_r0, _4bit_Decoder_r1, _4bit_Decoder_r2, _4bit_Decoder_r3, _4bit_Decoder_r4,
       _4bit_Decoder_r5, _4bit_Decoder_r6, _4bit_Decoder_r7, _4bit_Decoder_r8, _4bit_Decoder_r9,
       _4bit_Decoder_r10, _4bit_Decoder_r11, _4bit_Decoder_r12, _4bit_Decoder_r13, _4bit_Decoder_r14,
       _4bit_Decoder_r15, and_1_out, and_2_out, and_3_out, and_4_out, and_5_out, and_6_out, and_7_out,
       and_8_out, and_9_out, and_10_out, and_11_out, and_12_out, and_13_out, and_14_out, and_15_out,
       multiplexer_1_out;
  wire [31:0] multiplexer_2_out, subtractor_1_out;

  Decoder _4bit_Decoder (
    .in_1(A3), .R0(_4bit_Decoder_r0), .R1(_4bit_Decoder_r1), .R2(_4bit_Decoder_r2), .R3(_4bit_Decoder_r3),
    .R4(_4bit_Decoder_r4), .R5(_4bit_Decoder_r5), .R6(_4bit_Decoder_r6), .R7(_4bit_Decoder_r7),
    .R8(_4bit_Decoder_r8), .R9(_4bit_Decoder_r9), .R10(_4bit_Decoder_r10), .R11(_4bit_Decoder_r11),
    .R12(_4bit_Decoder_r12), .R13(_4bit_Decoder_r13), .R14(_4bit_Decoder_r14), .R15(_4bit_Decoder_r15));
  Subtractor #(.width(32)) subtractor_1 (.a(R15), .b(32'h4), .out(subtractor_1_out));  // open: bin, bout
  and and_1 (and_1_out, _4bit_Decoder_r14, WE);
  and and_2 (and_2_out, _4bit_Decoder_r0, WE);
  and and_3 (and_3_out, _4bit_Decoder_r1, WE);
  and and_4 (and_4_out, _4bit_Decoder_r2, WE);
  and and_5 (and_5_out, _4bit_Decoder_r3, WE);
  and and_6 (and_6_out, _4bit_Decoder_r4, WE);
  and and_7 (and_7_out, _4bit_Decoder_r5, WE);
  and and_8 (and_8_out, _4bit_Decoder_r6, WE);
  and and_9 (and_9_out, _4bit_Decoder_r7, WE);
  and and_10 (and_10_out, _4bit_Decoder_r8, WE);
  and and_11 (and_11_out, _4bit_Decoder_r9, WE);
  and and_12 (and_12_out, _4bit_Decoder_r10, WE);
  and and_13 (and_13_out, _4bit_Decoder_r11, WE);
  and and_14 (and_14_out, _4bit_Decoder_r12, WE);
  and and_15 (and_15_out, _4bit_Decoder_r13, WE);
  Multiplexer #(.enable("false")) multiplexer_1 (
    .in0(and_1_out), .in1(1'b1), .out(multiplexer_1_out), .sel(BranchLink));
  Multiplexer #(.width(32), .enable("false")) multiplexer_2 (
    .in0(WD3), .in1(subtractor_1_out), .out(multiplexer_2_out), .sel(BranchLink));
  Register #(.width(32)) register_1 (.D(WD3), .en(and_2_out), .Q(R0), .clk(CLK), .clr(CLR));
  Register #(.width(32)) register_2 (.D(WD3), .en(and_3_out), .Q(R1), .clk(CLK), .clr(CLR));
  Register #(.width(32)) register_3 (.D(WD3), .en(and_4_out), .Q(R2), .clk(CLK), .clr(CLR));
  Register #(.width(32)) register_4 (.D(WD3), .en(and_5_out), .Q(R3), .clk(CLK), .clr(CLR));
  Register #(.width(32)) register_5 (.D(WD3), .en(and_6_out), .Q(R4), .clk(CLK), .clr(CLR));
  Register #(.width(32)) register_6 (.D(WD3), .en(and_7_out), .Q(R5), .clk(CLK), .clr(CLR));
  Register #(.width(32)) register_7 (.D(WD3), .en(and_8_out), .Q(R6), .clk(CLK), .clr(CLR));
  Register #(.width(32)) register_8 (.D(WD3), .en(and_9_out), .Q(R7), .clk(CLK), .clr(CLR));
  Register #(.width(32)) register_9 (.D(WD3), .en(and_10_out), .Q(R8), .clk(CLK), .clr(CLR));
  Register #(.width(32)) register_10 (.D(WD3), .en(and_11_out), .Q(R9), .clk(CLK), .clr(CLR));
  Register #(.width(32)) register_11 (.D(WD3), .en(and_12_out), .Q(R10), .clk(CLK), .clr(CLR));
  Register #(.width(32)) register_12 (.D(WD3), .en(and_13_out), .Q(R11), .clk(CLK), .clr(CLR));
  Register #(.width(32)) register_13 (.D(WD3), .en(and_14_out), .Q(R12), .clk(CLK), .clr(CLR));
  Register #(.width(32)) register_14 (.D(WD3), .en(and_15_out), .Q(R13), .clk(CLK), .clr(CLR));
  Register #(.width(32)) register_15 (.D(multiplexer_2_out), .en(multiplexer_1_out), .Q(R14), .clk(CLK), .clr(CLR));
  Multiplexer #(.select(4), .width(32), .enable("false")) multiplexer_3 (
    .in0(R0), .in1(R1), .in2(R2), .in3(R3), .in4(R4), .in5(R5), .in6(R6), .in7(R7), .in8(R8), .in9(R9),
    .in10(R10), .in11(R11), .in12(R12), .in13(R13), .in14(R14), .in15(R15), .out(out_16), .sel(A2));
  Multiplexer #(.select(4), .width(32), .enable("false")) multiplexer_4 (
    .in0(R0), .in1(R1), .in2(R2), .in3(R3), .in4(R4), .in5(R5), .in6(R6), .in7(R7), .in8(R8), .in9(R9),
    .in10(R10), .in11(R11), .in12(R12), .in13(R13), .in14(R14), .in15(R15), .out(out_13), .sel(A1));

  assign R15_2 = R15;
endmodule

module Decoder (
  input  [3:0] in_1,
  output R0,
  output R1,
  output R2,
  output R3,
  output R4,
  output R5,
  output R6,
  output R7,
  output R8,
  output R9,
  output R10,
  output R11,
  output R12,
  output R13,
  output R14,
  output R15
);

  // Probe on in_1
  and and_1 (R0, ~in_1[0], ~in_1[1], ~in_1[2], ~in_1[3]);  // AND_Gate
  and and_2 (R1, in_1[0], ~in_1[1], ~in_1[2], ~in_1[3]);  // AND_Gate
  and and_3 (R2, ~in_1[0], in_1[1], ~in_1[2], ~in_1[3]);  // AND_Gate
  and and_4 (R3, in_1[0], in_1[1], ~in_1[2], ~in_1[3]);  // AND_Gate
  and and_5 (R4, ~in_1[0], ~in_1[1], in_1[2], ~in_1[3]);  // AND_Gate
  and and_6 (R5, in_1[0], ~in_1[1], in_1[2], ~in_1[3]);  // AND_Gate
  and and_7 (R6, ~in_1[0], in_1[1], in_1[2], ~in_1[3]);  // AND_Gate
  and and_8 (R7, in_1[0], in_1[1], in_1[2], ~in_1[3]);  // AND_Gate
  and and_9 (R8, ~in_1[0], ~in_1[1], ~in_1[2], in_1[3]);  // AND_Gate
  and and_10 (R9, in_1[0], ~in_1[1], ~in_1[2], in_1[3]);  // AND_Gate
  and and_11 (R10, ~in_1[0], in_1[1], ~in_1[2], in_1[3]);  // AND_Gate
  and and_12 (R11, in_1[0], in_1[1], ~in_1[2], in_1[3]);  // AND_Gate
  and and_13 (R12, ~in_1[0], ~in_1[1], in_1[2], in_1[3]);  // AND_Gate
  and and_14 (R13, in_1[0], ~in_1[1], in_1[2], in_1[3]);  // AND_Gate
  and and_15 (R14, ~in_1[0], in_1[1], in_1[2], in_1[3]);  // AND_Gate
  and and_16 (R15, in_1[0], in_1[1], in_1[2], in_1[3]);
endmodule

module Inst_mem (
  input  [1:0] Selector,
  input  [31:0] A,
  output [31:0] RD
);

  wire [23:0] divider_1_out;
  wire [31:0] rom_1_data, rom_2_data, rom_3_data, rom_4_data;

  Divider #(.width(24)) divider_1 (.a(A[23:0]), .b(24'h4), .out(divider_1_out));  // open: upper, rem
  ROM #(.addrWidth(24), .dataWidth(32)) rom_1 (.addr(divider_1_out), .data(rom_1_data), .sel(1'b1));
  ROM #(.addrWidth(24), .dataWidth(32)) rom_2 (.addr(divider_1_out), .data(rom_2_data), .sel(1'b1));
  ROM #(.addrWidth(24), .dataWidth(32)) rom_3 (.addr(divider_1_out), .data(rom_3_data), .sel(1'b1));
  ROM #(.addrWidth(24), .dataWidth(32)) rom_4 (.addr(divider_1_out), .data(rom_4_data), .sel(1'b1));
  Multiplexer #(.select(2), .width(32), .enable("false")) multiplexer_1 (
    .in0(rom_1_data), .in1(rom_2_data), .in2(rom_3_data), .in3(rom_4_data), .out(RD), .sel(Selector));

  // Notes on the sheet:
  //   contents of rom_1 (hex, n*v repeats v):
  //   e3a0dc01 e24dd004 e3a00002 e58d0000 e24dd004 e3a00003 e58d0000 e24dd004 e3a00004 e58d0000 e24dd004
  //   e3a00000 e2400003 e58d0000 e24dd004 e3a00009 e58d0000 e1a0000d e3a01005 eb000000 eafffffe e3a02000
  //   e3a03000 e1520001 a000004 e5904000 e0833004 e2822001 e2800004 eafffff8 e1a00003 e12fff1e
  //   contents of rom_2 (hex, n*v repeats v):
  //   e3a0dc01 e24dd004 e3a00002 e58d0000 e24dd004 e3a00002 e58d0000 e24dd004 e3a00025 e58d0000 e24dd004
  //   e3a00009 e58d0000 e24dd004 e3a00004 e58d0000 e1a0000d e3a01005 e24dd004 e58d4000 e24dd004 e58d5000
  //   e3a02000 e5903000 eb000000 eafffffe e1520001 a000005 e5904000 e2800004 e1540003 c1a03004 e2822001
  //   eafffff7 e59d5000 e28dd004 e59d4000 e28dd004 e1a00003 e12fff1e
  //   contents of rom_3 (hex, n*v repeats v):
  //   e3a0dc01 e3a00013 eb000000 eafffffe e24dd004 e58d4000 e24dd004 e58d5000 e3a01000 e3a02001 e3a03000
  //   e3a04001 e3500000 a00000a e3500001 a000006 e1540000 ca000006 e0813002 e1a02001 e1a01003 e2844001
  //   eafffff8 e3a03001 affffff e59d5000 e28dd004 e59d4000 e28dd004 e1a00003 e12fff1e
  //   contents of rom_4 (hex, n*v repeats v):
  //   e3a0dc01 e3a00006 eb000000 eafffffe e24dd004 e58d4000 e24dd004 e58d5000 e24dd004 e58d6000 e24dd004
  //   e58de000 e3500002 a000005 ca000004 e3500001 3a00001 e3500000 3a00000 ea000007 e1a06000 e2400001
  //   ebffffec e1a04000 e2460002 ebffffe9 e1a05000 e0840005 e59de000 e28dd004 e59d6000 e28dd004 e59d5000
  //   e28dd004 e59d4000 e28dd004 e12fff1e
endmodule

module Extend (
  input  [1:0] in_1,
  input  [23:0] in_2,
  output [31:0] out_3
);

  wire [31:0] bit_extender_1_out, bit_extender_2_out, bit_extender_3_out, shifter_1_out;

  assign bit_extender_1_out = {{8{in_2[23]}}, in_2};  // Bit_Extender bit_extender_1
  assign bit_extender_2_out = {{24{1'b0}}, in_2[7:0]};  // Bit_Extender bit_extender_2
  assign bit_extender_3_out = {{20{in_2[11]}}, in_2[11:0]};  // Bit_Extender bit_extender_3
  Shifter #(.width(32)) shifter_1 (.in(bit_extender_1_out), .\dist (5'b00010), .out(shifter_1_out));
  Multiplexer #(.select(2), .width(32), .enable("false")) multiplexer_1 (
    .in0(bit_extender_2_out), .in1(bit_extender_3_out), .in2(shifter_1_out), .out(out_3), .sel(in_1));  // open: in3
endmodule

module Data__Mem (
  input  CLK,
  input  [31:0] in_2,
  input  [31:0] in_3,
  input  WE,
  input  CLR,
  output [31:0] out_6
);

  wire not_1_out;

  not not_1 (not_1_out, WE);
  RAM #(.addrWidth(24), .dataWidth(32), .bus("separate")) ram_1 (
    .addr(in_2[23:0]), .din(in_3), .data(out_6), .str(WE), .sel(1'b1), .clk(CLK), .ld(not_1_out), .clr(CLR));
endmodule

module Control (
  input  CLK,
  input  [3:0] COND,
  input  [1:0] OP,
  input  [5:0] Funct,
  input  [3:0] RD,
  input  [23:0] BX,
  input  Z,
  input  N,
  input  C,
  input  V,
  input  CLR,
  output PCSrc,
  output MemReg,
  output MemW,
  output [1:0] IMMsrc,
  output RegWrite,
  output [1:0] REGSrc,
  output AlUsrc,
  output [1:0] AlUControl,
  output Do_Mov,
  output BranchLink,
  output BX_2
);

  wire alu_decoder_1_nowrite, c_main_decoder_1_aluop, c_main_decoder_1_branch, c_main_decoder_1_memw,
       c_main_decoder_1_regw, pc_logic_1_pcs;
  wire [1:0] alu_decoder_1_flagw;

  PC_logic pc_logic_1 (.RD(RD), .RegW(c_main_decoder_1_regw), .Branch(c_main_decoder_1_branch), .PCS(pc_logic_1_pcs));
  and and_1 (BX_2, ~BX[23], ~BX[22], ~BX[21], BX[20], ~BX[19], ~BX[18], BX[17], ~BX[16], BX[15], BX[14], BX[13], BX[12], BX[11], BX[10], BX[9], BX[8], BX[7], BX[6], BX[5], BX[4], ~BX[3], ~BX[2], ~BX[1], BX[0]);  // AND_Gate
  C_Main_Decoder c_main_decoder_1 (
    .OP(OP), .Funct(Funct), .Branch(c_main_decoder_1_branch), .MemToReg(MemReg),
    .MemW(c_main_decoder_1_memw), .ALUSrc(AlUsrc), .ImmSrc(IMMsrc), .RegW(c_main_decoder_1_regw),
    .RegSrc(REGSrc), .ALUop(c_main_decoder_1_aluop), .BranchLink(BranchLink));
  C_cond_logic c_cond_logic_1 (
    .PCS(pc_logic_1_pcs), .RegW(c_main_decoder_1_regw), .NoWrite(alu_decoder_1_nowrite),
    .MemW(c_main_decoder_1_memw), .FlagW(alu_decoder_1_flagw), .Cond(COND), .Z(Z), .N(N), .C(C), .V(V),
    .CLK(CLK), .CLR(CLR), .PCSrc(PCSrc), .RegWrite(RegWrite), .MemWrite(MemW));
  ALU_Decoder alu_decoder_1 (
    .ALUop(c_main_decoder_1_aluop), .Funct(Funct), .ALUControl(AlUControl), .FlagW(alu_decoder_1_flagw),
    .NoWrite(alu_decoder_1_nowrite), .Do_Mov(Do_Mov));
endmodule

module C_Main_Decoder (
  input  [1:0] OP,
  input  [5:0] Funct,
  output Branch,
  output BranchLink,
  output MemToReg,
  output MemW,
  output ALUSrc,
  output [1:0] ImmSrc,
  output RegW,
  output [1:0] RegSrc,
  output ALUop
);

  wire _00_out, _01_2_out, _01_out, _10_out, DPI_out, DPR_out, not_1_out, not_2_out, not_3_out, not_4_out,
       or_4_out;

  and DPR (DPR_out, ~OP[0], ~OP[1], ~Funct[5]);  // AND_Gate
  and DPI (DPI_out, ~OP[0], ~OP[1], Funct[5]);  // AND_Gate
  and STR (MemW, OP[0], ~OP[1], ~Funct[0]);  // AND_Gate
  and B (Branch, ~OP[0], Funct[5], OP[1]);  // AND_Gate
  and LDR (MemToReg, OP[0], ~OP[1], Funct[0]);  // AND_Gate
  or or_1 (ALUSrc, DPI_out, MemW, MemToReg, Branch);
  and _00 (_00_out, DPI_out, ~MemW, ~MemToReg, ~Branch);  // AND_Gate
  and _01 (_01_out, ~DPI_out, MemW, ~MemToReg, ~Branch);  // AND_Gate
  and _01_2 (_01_2_out, ~DPI_out, ~MemW, MemToReg, ~Branch);  // AND_Gate
  and _10 (_10_out, ~DPI_out, ~MemW, ~MemToReg, Branch);  // AND_Gate
  or or_2 (RegW, DPR_out, DPI_out, MemToReg);
  or or_3 (ALUop, DPR_out, DPI_out);
  not not_1 (not_1_out, _00_out);
  not not_2 (not_2_out, _10_out);
  or or_4 (or_4_out, _01_out, _01_2_out);
  Multiplexer #(.enable("false")) multiplexer_1 (.in0(1'b0), .in1(1'b1), .out(RegSrc[0]), .sel(OP[1]));
  and and_1 (BranchLink, Branch, Funct[4]);
  Multiplexer #(.select(2), .enable("false")) multiplexer_2 (
    .in0(not_1_out), .in1(or_4_out), .in2(not_2_out), .in3(not_2_out), .out(ImmSrc[0]), .sel(OP));
  not not_3 (not_3_out, _00_out);
  not not_4 (not_4_out, or_4_out);
  Multiplexer #(.enable("false")) multiplexer_3 (.in0(1'b0), .in1(1'b1), .out(RegSrc[1]), .sel(OP[0]));
  Multiplexer #(.select(2), .enable("false")) multiplexer_4 (
    .in0(not_3_out), .in1(not_4_out), .in2(_10_out), .in3(_10_out), .out(ImmSrc[1]), .sel(OP));
endmodule

module ALU_Decoder (
  input  ALUop,
  input  [5:0] Funct,
  output [1:0] ALUControl,
  output Do_Mov,
  output [1:0] FlagW,
  output NoWrite
);

  wire ADD_out, and_2_out, AND_out, CMP_out, ORR_out, SUB_out;
  wire [1:0] multiplexer_1_out, multiplexer_2_out, multiplexer_3_out, multiplexer_4_out, multiplexer_6_out,
       multiplexer_7_out;

  and ADD (ADD_out, ALUop, ~Funct[4], Funct[3], ~Funct[2], ~Funct[1]);  // AND_Gate
  Multiplexer #(.width(2), .enable("false")) multiplexer_1 (
    .in0(2'b00), .in1(2'b00), .out(multiplexer_1_out), .sel(ADD_out));
  and SUB (SUB_out, ALUop, ~Funct[4], ~Funct[3], Funct[2], ~Funct[1]);  // AND_Gate
  Multiplexer #(.width(2), .enable("false")) multiplexer_2 (
    .in0(multiplexer_1_out), .in1(2'b01), .out(multiplexer_2_out), .sel(SUB_out));
  and ORR (ORR_out, ALUop, Funct[4], Funct[3], ~Funct[2], ~Funct[1]);  // AND_Gate
  and AND (AND_out, ALUop, ~Funct[4], ~Funct[3], ~Funct[2], ~Funct[1]);  // AND_Gate
  Multiplexer #(.width(2), .enable("false")) multiplexer_3 (
    .in0(multiplexer_2_out), .in1(2'b10), .out(multiplexer_3_out), .sel(AND_out));
  and CMP (CMP_out, ALUop, Funct[4], ~Funct[3], Funct[2], ~Funct[1]);  // AND_Gate
  Multiplexer #(.width(2), .enable("false")) multiplexer_4 (
    .in0(multiplexer_3_out), .in1(2'b11), .out(multiplexer_4_out), .sel(ORR_out));
  Multiplexer #(.width(2), .enable("false")) multiplexer_5 (
    .in0(multiplexer_4_out), .in1(2'b01), .out(ALUControl), .sel(CMP_out));
  and Mov (Do_Mov, ALUop, Funct[4], Funct[3], ~Funct[2], Funct[1]);  // AND_Gate
  Multiplexer #(.select(2), .width(2), .enable("false")) multiplexer_6 (
    .in0(2'b11), .in1(2'b11), .in2(2'b10), .in3(2'b10), .out(multiplexer_6_out), .sel(ALUControl));
  and and_2 (and_2_out, ALUop, Funct[0]);
  Multiplexer #(.width(2), .enable("false")) multiplexer_7 (
    .in0(2'b00), .in1(multiplexer_6_out), .out(multiplexer_7_out), .sel(and_2_out));
  and and_3 (NoWrite, and_2_out, CMP_out);
  Multiplexer #(.width(2), .enable("false")) multiplexer_8 (
    .in0(multiplexer_7_out), .in1(2'b11), .out(FlagW), .sel(NoWrite));
endmodule

module C_cond_logic (
  input  PCS,
  input  RegW,
  input  NoWrite,
  input  MemW,
  input  [1:0] FlagW,
  input  [3:0] Cond,
  input  Z,
  input  N,
  input  C,
  input  V,
  input  CLK,
  input  CLR,
  output PCSrc,
  output RegWrite,
  output MemWrite
);

  wire [1:0] and_1_out, check_cond_1_condex, register_1_q, register_2_q;

  Register #(.width(2)) register_1 (.D({N, Z}), .en(and_1_out[1]), .Q(register_1_q), .clk(CLK), .clr(CLR));
  Register #(.width(2)) register_2 (.D({C, V}), .en(and_1_out[0]), .Q(register_2_q), .clk(CLK), .clr(CLR));
  assign and_1_out = FlagW & check_cond_1_condex;  // AND_Gate and_1, 2 bits wide
  Check_Cond check_cond_1 (.NZ(register_1_q), .CV(register_2_q), .Cond(Cond), .CondEx(check_cond_1_condex[0]));
  and and_2 (PCSrc, PCS, check_cond_1_condex[0]);
  and and_3 (RegWrite, RegW, ~NoWrite, check_cond_1_condex[0]);  // AND_Gate
  and and_4 (MemWrite, MemW, check_cond_1_condex[0]);
endmodule

module Check_Cond (
  input  [1:0] NZ,
  input  [1:0] CV,
  input  [3:0] Cond,
  output CondEx
);

  wire AL_out, and_1_out, EQ_out, GE_out, GT_out, LE_out, LT_out, NE_2_out, NE_out;

  and EQ (EQ_out, CV[1], NZ[0], ~NZ[1], ~CV[0], ~Cond[3], ~Cond[2], ~Cond[1], ~Cond[0]);  // AND_Gate
  and NE (NE_out, ~Cond[3], ~Cond[2], ~Cond[1], Cond[0], ~1'b0, ~1'b0, ~1'b0, 1'b1);  // AND_Gate
  and and_1 (and_1_out, NE_2_out, NE_out);
  not NE_2 (NE_2_out, EQ_out);
  and LE (LE_out, CV[1], NZ[0], ~NZ[1], ~CV[0], Cond[3], Cond[2], ~Cond[1], Cond[0]);  // AND_Gate
  and LT (LT_out, ~CV[1], ~NZ[0], NZ[1], ~CV[0], Cond[3], ~Cond[2], Cond[1], Cond[0]);  // AND_Gate
  or or_1 (CondEx, EQ_out, LE_out, LT_out, and_1_out, GT_out, GE_out, AL_out);
  and GT (GT_out, ~NZ[0], ~NZ[1], ~CV[0], CV[1], Cond[3], Cond[2], ~Cond[1], ~Cond[0]);  // AND_Gate
  and GE (GE_out, CV[1], NZ[0], ~NZ[1], ~CV[0], Cond[3], ~Cond[2], Cond[1], ~Cond[0]);  // AND_Gate
  and AL (AL_out, Cond[3], Cond[2], Cond[1], ~Cond[0], 1'b1, 1'b1, 1'b1, ~1'b0);  // AND_Gate
endmodule

module PC_logic (
  input  [3:0] RD,
  input  RegW,
  input  Branch,
  output PCS
);

  wire and_1_out, and_2_out;

  and and_1 (and_1_out, 1'b1, RD[0], RD[1], RD[2], RD[3]);
  and and_2 (and_2_out, and_1_out, RegW);
  or or_1 (PCS, and_2_out, Branch);
endmodule

module PC (
  input  BX,
  input  CLK,
  input  [31:0] R14,
  input  [31:0] D,
  input  CLR,
  output [31:0] out_6
);

  wire [31:0] multiplexer_1_out;

  Multiplexer #(.width(32), .enable("false")) multiplexer_1 (.in0(D), .in1(R14), .out(multiplexer_1_out), .sel(BX));
  Register #(.width(32)) PC (.D(multiplexer_1_out), .en(1'b1), .Q(out_6), .clk(CLK), .clr(CLR));
endmodule
