// Logisim project Logic.circ as structural Verilog
module _1_bit_adder (
  input  A,
  input  B,
  input  Cin,
  output SUM,
  output Cout
);

  wire and_1_out, and_2_out, and_3_out, and_4_out, and_5_out, and_6_out, and_7_out, and_8_out;

  and and_1 (and_1_out, ~A, ~B, Cin);  // AND_Gate
  and and_2 (and_2_out, ~A, B, ~Cin);  // AND_Gate
  and and_3 (and_3_out, A, ~B, ~Cin);  // AND_Gate
  and and_4 (and_4_out, A, B, Cin);
  and and_5 (and_5_out, ~A, B, Cin);  // AND_Gate
  and and_6 (and_6_out, A, ~B, Cin);  // AND_Gate
  and and_7 (and_7_out, A, B, ~Cin);  // AND_Gate
  and and_8 (and_8_out, A, B, Cin);
  or or_1 (SUM, and_1_out, and_2_out, and_3_out, and_4_out);
  or or_2 (Cout, and_5_out, and_6_out, and_7_out, and_8_out);
endmodule

module _4_bit_adder (
  input  Cin,
  input  [3:0] D4_1,
  input  [3:0] D4_2,
  output [3:0] total,
  output Cout
);

  wire n1_bit_adder_1_cout, n1_bit_adder_2_cout, n1_bit_adder_3_cout;

  // Probe on D4_1
  // Probe on D4_2
  _1_bit_adder u_1_bit_adder_1 (.SUM(total[0]), .Cout(n1_bit_adder_1_cout), .A(D4_2[0]), .B(D4_1[0]), .Cin(Cin));
  _1_bit_adder u_1_bit_adder_2 (
    .SUM(total[1]), .Cout(n1_bit_adder_2_cout), .A(D4_2[1]), .B(D4_1[1]), .Cin(n1_bit_adder_1_cout));
  _1_bit_adder u_1_bit_adder_3 (
    .SUM(total[2]), .Cout(n1_bit_adder_3_cout), .A(D4_2[2]), .B(D4_1[2]), .Cin(n1_bit_adder_2_cout));
  _1_bit_adder u_1_bit_adder_4 (.SUM(total[3]), .Cout(Cout), .A(D4_2[3]), .B(D4_1[3]), .Cin(n1_bit_adder_3_cout));
  // Probe on total
endmodule

module SR_Latch_clr (
  input  in_1,
  input  in_2,
  input  in_3,
  output Q,
  output NotQ
);

  wire nor_1_out, nor_2_out;

  nor nor_1 (nor_1_out, in_1, NotQ);
  nor nor_2 (nor_2_out, in_2, Q);
  and and_1 (Q, nor_1_out, ~in_3);  // AND_Gate
  or or_1 (NotQ, nor_2_out, in_3);
endmodule

module D_latch_clr (
  input  CLK,
  input  D,
  input  Clear,
  output Q,
  output Qnot
);

  wire and_1_out, and_2_out;

  and and_1 (and_1_out, ~D, CLK);  // AND_Gate
  and and_2 (and_2_out, D, CLK);
  SR_Latch_clr sr_latch_clr_1 (.in_1(and_1_out), .in_2(and_2_out), .in_3(Clear), .Q(Q), .NotQ(Qnot));
endmodule

module D_flip_flop (
  input  CLK,
  input  D,
  input  CLR,
  output Q
);

  wire d_latch_clr_1_q, not_1_out;

  D_latch_clr d_latch_clr_1 (.CLK(not_1_out), .D(D), .Clear(CLR), .Q(d_latch_clr_1_q));  // open: Qnot
  not not_1 (not_1_out, CLK);
  D_latch_clr d_latch_clr_2 (.CLK(CLK), .D(d_latch_clr_1_q), .Clear(CLR), .Q(Q));  // open: Qnot
endmodule

module _1_bit_reg (
  input  CLK,
  input  D,
  input  CLR,
  input  WriteEnabled,
  output Q
);

  wire and_1_out;

  and and_1 (and_1_out, CLK, WriteEnabled);
  D_flip_flop d_flip_flop_1 (.CLK(and_1_out), .D(D), .CLR(CLR), .Q(Q));
endmodule

module _4_bit_reg (
  input  CLK,
  input  [3:0] Data,
  input  Write_enabled,
  input  Clr,
  output [3:0] out_5
);

  _1_bit_reg u_1_bit_reg_1 (.CLK(CLK), .D(Data[0]), .CLR(Clr), .WriteEnabled(Write_enabled), .Q(out_5[0]));
  _1_bit_reg u_1_bit_reg_2 (.CLK(CLK), .D(Data[1]), .CLR(Clr), .WriteEnabled(Write_enabled), .Q(out_5[1]));
  _1_bit_reg u_1_bit_reg_3 (.CLK(CLK), .D(Data[2]), .CLR(Clr), .WriteEnabled(Write_enabled), .Q(out_5[2]));
  _1_bit_reg u_1_bit_reg_4 (.CLK(CLK), .D(Data[3]), .CLR(Clr), .WriteEnabled(Write_enabled), .Q(out_5[3]));
endmodule

module _4_bit_counter (
  input  CLK,
  input  clr,
  output [3:0] counter
);

  wire [3:0] n4_bit_adder_1_total;

  _4_bit_reg u_4_bit_reg_1 (.CLK(CLK), .Data(n4_bit_adder_1_total), .Write_enabled(1'b1), .Clr(clr), .out_5(counter));
  _4_bit_adder u_4_bit_adder_1 (
    .D4_1(counter), .D4_2(4'b0001), .total(n4_bit_adder_1_total), .Cin(1'b0));  // open: Cout
  // Probe on counter
endmodule

module _8_bit_reg (
  input  CLK,
  input  [7:0] in_2,
  input  Write_enabled,
  input  Clr,
  output [7:0] out_5
);

  _4_bit_reg u_4_bit_reg_1 (.CLK(CLK), .Data(in_2[3:0]), .Write_enabled(Write_enabled), .Clr(Clr), .out_5(out_5[3:0]));
  _4_bit_reg u_4_bit_reg_2 (.CLK(CLK), .Data(in_2[7:4]), .Write_enabled(Write_enabled), .Clr(Clr), .out_5(out_5[7:4]));
endmodule

module _32_bit_adder (
  input  in_1,
  input  [31:0] in_2,
  input  [31:0] in_3,
  output [31:0] total,
  output out_5
);

  wire n4_bit_adder_1_cout, n4_bit_adder_2_cout, n4_bit_adder_3_cout, n4_bit_adder_4_cout,
       n4_bit_adder_5_cout, n4_bit_adder_6_cout, n4_bit_adder_7_cout;

  _4_bit_adder u_4_bit_adder_1 (
    .D4_1(in_2[3:0]), .D4_2(in_3[3:0]), .total(total[3:0]), .Cin(in_1), .Cout(n4_bit_adder_1_cout));
  _4_bit_adder u_4_bit_adder_2 (
    .D4_1(in_2[7:4]), .D4_2(in_3[7:4]), .total(total[7:4]), .Cin(n4_bit_adder_1_cout),
    .Cout(n4_bit_adder_2_cout));
  _4_bit_adder u_4_bit_adder_3 (
    .D4_1(in_2[11:8]), .D4_2(in_3[11:8]), .total(total[11:8]), .Cin(n4_bit_adder_2_cout),
    .Cout(n4_bit_adder_3_cout));
  _4_bit_adder u_4_bit_adder_4 (
    .D4_1(in_2[15:12]), .D4_2(in_3[15:12]), .total(total[15:12]), .Cin(n4_bit_adder_3_cout),
    .Cout(n4_bit_adder_4_cout));
  _4_bit_adder u_4_bit_adder_5 (
    .D4_1(in_2[19:16]), .D4_2(in_3[19:16]), .total(total[19:16]), .Cin(n4_bit_adder_4_cout),
    .Cout(n4_bit_adder_5_cout));
  _4_bit_adder u_4_bit_adder_6 (
    .D4_1(in_2[23:20]), .D4_2(in_3[23:20]), .total(total[23:20]), .Cin(n4_bit_adder_5_cout),
    .Cout(n4_bit_adder_6_cout));
  _4_bit_adder u_4_bit_adder_7 (
    .D4_1(in_2[27:24]), .D4_2(in_3[27:24]), .total(total[27:24]), .Cin(n4_bit_adder_6_cout),
    .Cout(n4_bit_adder_7_cout));
  _4_bit_adder u_4_bit_adder_8 (
    .D4_1(in_2[31:28]), .D4_2(in_3[31:28]), .total(total[31:28]), .Cin(n4_bit_adder_7_cout), .Cout(out_5));
endmodule

module mux (
  input  A,
  input  B,
  input  S,
  output out_4
);

  wire and_1_out, and_2_out, and_3_out, and_4_out;

  and and_1 (and_1_out, ~A, B, S);  // AND_Gate
  and and_2 (and_2_out, A, ~B, ~S);  // AND_Gate
  or or_1 (out_4, and_1_out, and_2_out, and_3_out, and_4_out);
  and and_3 (and_3_out, A, B, ~S);  // AND_Gate
  and and_4 (and_4_out, A, B, S);
endmodule
